# Fritzing sketch Telemetry (saved by Fritzing 0.9.9b)
circuit board: 10.4cm x 11.8cm
breadboards: 1

parts:
  Part1 = InvenSense MPU6050
  Part3 = Adafruit MicroSD card breakout board [part_number="Adafruit #254"]
  Part5 = Adafruit DS1307 RTC [part_number="Adafruit #3296"]
  Mod1 = RYLR896 [package=THT]
  Part6 = BME280 Breakout
  Part7 = Arduino Mega 2560 (Rev3)
  U2 = Voltage Regulator - 3.3V [package="TO220 [THT]"]
  U1 = Voltage Regulator - 3.3V [package="TO220 [THT]"]
  Part4 = Adafruit Ultimate GPS v3 [part_number="Adafruit #746"]

nets (from the schematic view):
  3.3V: Part1.VDD, Part1.VIO, Part3.+3V3, Mod1.pin1, Part6.3.3V, U1.output_voltage, Part4.3.3V
  GND: Part1.GND, Part3.GND, Part5.GND, Mod1.pin5, Part6.GND, Part7.GND, U2.GND, U1.GND, Part4.GND
  N1: Part1.SCL, Part5.SCL, Part6.SCK/SCL, Part7.D21/SCL
  N2: Part1.SDA, Part5.SDA, Part6.SDI/SDA, Part7.D20/SDA, Part7.SDA
  5V: Part5.5V, Part7.5V, U1.input_voltage
  N3: Mod1.pin3#2, U2.output_voltage
  N4: Part7.D19/RX1, Part4.TX
  N5: Part7.D18/TX1, Part4.RX
  N6: Part7.D1_TX0, U2.input_voltage

custom parts:
  InvenSense MPU6050: The InvenSense MPU-6050 sensor contains a MEMS accelerometer and a MEMS gyro in a single chip. It is very accurate, as it contains 16-bits analog to digital conversion hardware for each channel. Therefor it captures the x, y, and z channel at the same time. The sensor uses the I2C-bus to interface with the Arduino.
  Adafruit MicroSD card breakout board: Not just a simple breakout board, this microSD adapter goes the extra mile - designed for ease of use. Onboard 5v->3v regulator provides 150mA for power-hungry cards 3v level shifting means you can use this with ease on either 3v or 5v systems Uses a proper level shifting chip, not resistors: less problems, and faster read/write access Use 3 or 4 digital pins to read and write 2Gb+ of storage!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
  Adafruit DS1307 RTC: This is a great battery-backed real time clock (RTC) that allows your microcontroller project to keep track of time even if it is reprogrammed, or if the power is lost. Perfect for datalogging, clock-building, time stamping, timers and alarms, etc. Equipped with PCF8523 RTC - it can run from 3.3V or 5V power & logic! Works great with an Arduino using our RTC library, with CircuitPython or with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
  RYLR896: RYLR896 UART Interface 868/915mhz LORA Transceiver Module
  Adafruit Ultimate GPS v3: We carry a few different GPS modules here in the Adafruit shop, but none that satisfied our every desire - that's why we designed this little GPS breakout board. We believe this is the Ultimate GPS module, so we named it that. It's got everything you want and more: -165 dBm sensitivity, 10 Hz updates, 66 channels 5V friendly design and only 20mA current draw Breadboard friendly + two mounting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
